// Logisim project alu.circ as structural Verilog: 1 circuit, main circuit alu
module alu (
  input  [31:0] A,
  input  [31:0] B,
  input  [3:0] ALUSel,
  input  in_4,
  output [31:0] Result
);

  wire comparator_1_eq;
  wire [4:0] bit_extender_2_out, bit_extender_3_out, bit_extender_4_out;
  wire [31:0] addGate, andGate, bseler, muler, mulher, mulhuer, orGate, sller, slt, sraer, srler, suber,
       xorGate;

  Adder #(.width(32)) adder_1 (.a(A), .b(B), .out(addGate));  // open: cin, cout
  assign andGate = A & B;  // AND_Gate and_1, 32 bits wide
  assign orGate = A | B;  // OR_Gate or_1, 32 bits wide
  Multiplier #(.width(32)) multiplier_1 (.a(A), .b(B), .out(muler));  // open: cin, cout
  Multiplier #(.width(32)) multiplier_2 (.a(A), .b(B), .out(mulher));  // open: cin, cout
  Subtractor #(.width(32)) subtractor_1 (.a(A), .b(B), .out(suber));  // open: bin, bout
  Multiplier #(.width(32)) multiplier_3 (.a(A), .b(B), .out(mulhuer));  // open: cin, cout
  assign xorGate = A ^ B;  // XOR_Gate xor_1, 32 bits wide
  Comparator #(.width(32)) comparator_1 (.a(A), .b(B), .eq(comparator_1_eq));  // open: gt, lt
  Multiplexer #(.enable("false"), .width(32)) multiplexer_1 (.in0(A), .in1(B), .out(bseler), .sel(in_4));
  assign slt = {{31{comparator_1_eq}}, comparator_1_eq};  // Bit_Extender bit_extender_1
  Bit_Extender #(.in_width(32), .out_width(5)) bit_extender_2 (.in(B), .out(bit_extender_2_out));
  Bit_Extender #(.in_width(32), .out_width(5)) bit_extender_3 (.in(B), .out(bit_extender_3_out));
  Bit_Extender #(.in_width(32), .out_width(5)) bit_extender_4 (.in(B), .out(bit_extender_4_out));
  Shifter #(.shift("lr"), .width(32)) shifter_1 (.in(A), .\dist (bit_extender_2_out), .out(srler));
  Shifter #(.shift("ar"), .width(32)) shifter_2 (.in(A), .\dist (bit_extender_3_out), .out(sraer));
  Shifter #(.width(32)) shifter_3 (.in(A), .\dist (bit_extender_4_out), .out(sller));
  Multiplexer #(.enable("false"), .select(4), .width(32)) multiplexer_2 (
    .in0(addGate), .in1(andGate), .in2(orGate), .in3(xorGate), .in4(srler), .in5(sraer), .in6(sller),
    .in7(slt), .in10(muler), .in11(mulhuer), .in12(suber), .in13(bseler), .in14(mulher), .out(Result),
    .sel(ALUSel));  // open: in8, in9, in15

  // Notes on the sheet:
  //   INPUTS to your circuit
  //   DON'T CHANGE THE LOCATIONS OF THE INPUTS AND OUTPUTS!
  //   OUTPUT from your circuit
endmodule
